// Logisim project I.circ as structural Verilog: 1 circuit, main circuit I kolo
module I_kolo (
  input  a,
  input  b,
  input  c,
  input  d,
  input  e,
  output x
);

  wire and_1_out, and_2_out, and_4_out, not_1_out, not_2_out, not_3_out, not_4_out;

  not not_1 (not_1_out, b);
  and and_1 (and_1_out, a, not_1_out);
  not not_2 (not_2_out, c);
  not not_3 (not_3_out, d);
  not not_4 (not_4_out, e);
  and and_2 (and_2_out, and_1_out, not_2_out);
  and and_3 (x, and_2_out, and_4_out);
  and and_4 (and_4_out, not_3_out, not_4_out);
endmodule
