// Logisim project NILI.circ as structural Verilog: 1 circuit, main circuit NILI kolo
module NILI_kolo (
  input  in_1,
  input  in_2,
  input  in_3,
  input  in_4,
  input  in_5,
  output out_6
);

  wire nor_1_out, nor_2_out, nor_3_out, nor_4_out, nor_5_out, nor_6_out, nor_7_out, nor_8_out, nor_9_out,
       nor_10_out, nor_11_out, nor_12_out, nor_13_out, nor_14_out, nor_16_out;

  nor nor_1 (nor_1_out, in_1, in_1);
  nor nor_2 (nor_2_out, in_2, in_2);
  nor nor_3 (nor_3_out, in_4, in_4);
  nor nor_4 (nor_4_out, in_5, in_5);
  nor nor_5 (nor_5_out, nor_2_out, nor_2_out);
  nor nor_6 (nor_6_out, in_3, in_3);
  nor nor_7 (nor_7_out, nor_1_out, nor_5_out);
  nor nor_8 (nor_8_out, nor_3_out, nor_3_out);
  nor nor_9 (nor_9_out, nor_4_out, nor_4_out);
  nor nor_10 (nor_10_out, nor_7_out, nor_7_out);
  nor nor_11 (nor_11_out, nor_6_out, nor_6_out);
  nor nor_12 (nor_12_out, nor_10_out, nor_11_out);
  nor nor_13 (nor_13_out, nor_8_out, nor_9_out);
  nor nor_14 (nor_14_out, nor_12_out, nor_12_out);
  nor nor_15 (out_6, nor_14_out, nor_16_out);
  nor nor_16 (nor_16_out, nor_13_out, nor_13_out);
endmodule
